// Logisim project Single_cycle_block.circ as structural Verilog: 1 circuit, main circuit main
module main (
  output [31:0] out_1,
  output [31:0] out_2,
  output [31:0] out_3,
  output [31:0] out_4,
  output [31:0] out_5,
  output [31:0] out_6,
  output [31:0] out_7,
  output [31:0] out_8,
  output [31:0] out_9,
  output [31:0] out_10,
  output [31:0] out_11,
  output [31:0] out_12,
  output [31:0] out_13,
  output [31:0] out_14,
  output [31:0] out_15,
  output [31:0] out_16,
  output [31:0] out_17,
  output [31:0] out_18,
  output [31:0] out_19,
  output [31:0] out_20,
  output [31:0] out_21,
  output [31:0] out_22,
  output [31:0] out_23,
  output [31:0] out_24,
  output [31:0] out_25,
  output [31:0] out_26,
  output [31:0] out_27,
  output [31:0] out_28,
  output [31:0] out_29,
  output [31:0] out_30,
  output [31:0] out_31,
  output [31:0] out_32
);

  wire clock_1_out, EXT_OP, Kill_1, Kill_2, less_falg, less_Unsign_falg, MEM_Read, MEM_Read_EX, MEM_Read_mem,
       MEM_Write, MEM_Write_EX, MEM_Write_mem, or_1_out, Reg_write, Reg_write_EX, reg_write_mem,
       reg_write_WB, SSET, SSET_EX, SSET_MEM, SSET_WB, Stall, WB, WB_EX, WB_mem, Zero_flag;
  wire [1:0] ALU_SRC, ALU_SRC_EX, Forwad_B, Forward_A, PC_SELC, Rd_SRC, Rd_SRC_EX, rd_src_mem, rd_src_WB;
  wire [3:0] func_4bit;
  wire [4:0] immd_L, immd_L_EX, RD_EX, rd_mem, rd_WB, Rs_EX, Rs_ID, Rt_EX, Rt_ID;
  wire [5:0] opcode;
  wire [9:0] ALU_OP, ALU_OP_EX;
  wire [10:0] immd_U_EX;
  wire [15:0] imm16, imm16_16bit_EX, imm16_16bit_mem, imm16_16bit_wb;
  wire [19:0] PC, PC_ID, PC_Plus_1, PC_Plus_1_EX, PC_Plus_1_ID, pc_plus_1_mem, PC_plus_1_WB;
  wire [31:0] ALU_res_EX, Alu_res_mem, bit_extender_2_out, bit_extender_3_out, bit_extender_4_out, BusA_ID,
       BUSB_EX, BusB_ID, BUSB_mem, BUSB_wb, imm16_32_mem, imm16_32_wb, immdL_immdU_EX, main_3_instruction,
       main_7_out_22, main_9_data_out, main_10_out_11, mem_2prev, multiplexer_1_out, multiplexer_2_out,
       multiplexer_4_out, multiplexer_5_out, multiplexer_6_out, multiplexer_7_out, WB_3Prev;
  wire [31:16] imm16_32_EX;

  Clock clock_1 (.out(clock_1_out));
  // Probe on out_1
  // Probe on out_15
  // Probe on out_29
  // Probe on out_2
  // Probe on out_16
  // Probe on out_30
  // Probe on BusB_ID
  // Probe on out_3
  // Probe on out_17
  // Probe on out_31
  // Probe on out_4
  // Probe on out_18
  // Probe on out_32
  // pc_new_main main_1: pin names not known; wires that end beside it: {imm16[15:9], func_4bit, imm16[4:0]}, BusA_ID, {imm16[15:9], func_4bit}, immd_L, PC_ID, Stall, PC_SELC, clock_1_out, PC, PC_Plus_1
  // Probe on out_5
  // Probe on out_19
  // Probe on out_6
  // Probe on out_7
  // Probe on out_20
  // Probe on opcode[4:0]
  // Probe on out_21
  // Probe on PC
  // Probe on out_8
  // Probe on out_22
  // Probe on out_9
  // Probe on out_23
  PC_Control_Unit_main main_2 (
    .in_1(Zero_flag), .in_2(less_falg), .in_3(less_Unsign_falg), .op_code_5bit(opcode[4:0]), .out_6(PC_SELC),
    .Kill_1(Kill_1), .Kill_2(Kill_2));
  // Probe on out_10
  // Probe on out_24
  // Probe on out_11
  // Probe on out_25
  // Probe on out_12
  // Probe on out_26
  // Probe on opcode
  or or_1 (or_1_out, Stall, Kill_1);
  // Probe on out_13
  // Probe on out_27
  // Probe on out_14
  // Probe on out_28
  main_control_unit main_control_unit_1 (
    .opcode(opcode), .reg_write(Reg_write), .sset(SSET), .ext_op(EXT_OP), .Rd_src(Rd_SRC), .alu_src(ALU_SRC),
    .mem_write(MEM_Read), .mem_read(MEM_Write), .wb(WB), .Stall(or_1_out));
  Instruction_Mem_main main_3 (.Address(PC), .Instruction(main_3_instruction));
  Multiplexer #(.width(32), .enable("false")) multiplexer_1 (
    .in0(main_3_instruction), .in1({32{1'b0}}), .out(multiplexer_1_out), .sel(Kill_2));
  // Probe on Rd_SRC
  // Probe on multiplexer_1_out
  if_id_main main_4 (
    .Instruction(multiplexer_1_out), .PC_plus_1(PC_Plus_1),
    .out_6({imm16[15:9], func_4bit, imm16[4:0], Rs_ID, immd_L, opcode}), .out_7(PC_Plus_1_ID),
    .in_5(clock_1_out), .stall(Stall), .PC(PC), .out_8(PC_ID));
  // Probe on {imm16[15:9], func_4bit, imm16[4:0], Rs_ID, immd_L, opcode}
  assign immdL_immdU_EX = {{16{immd_U_EX[10]}}, {immd_U_EX, immd_L_EX}};  // Bit_Extender bit_extender_1
  assign bit_extender_2_out = {{16{imm16[15]}}, {imm16[15:9], func_4bit, imm16[4:0]}};  // Bit_Extender bit_extender_2
  assign bit_extender_3_out = {{16{1'b0}}, {imm16[15:9], func_4bit, imm16[4:0]}};  // Bit_Extender bit_extender_3
  Forward_main main_5 (
    .Reg_Wr_EX(Reg_write_EX), .Reg_Wr_MEM(reg_write_mem), .Reg_Wr_WB(reg_write_WB), .Rs(Rs_ID), .Rt(Rt_ID),
    .Forwad_A(Forward_A), .Rd_EX(RD_EX), .Rd_MEM(rd_mem), .Rd_WB(rd_WB), .Stall(Stall),
    .MEM_Read_EX(MEM_Read_EX), .Forwad_B(Forwad_B));
  Multiplexer #(.width(32), .enable("false")) multiplexer_2 (
    .in0(bit_extender_2_out), .in1(bit_extender_3_out), .out(multiplexer_2_out), .sel(EXT_OP));
  // Probe on Stall
  // Probe on multiplexer_2_out
  // Probe on reg_write_WB
  // Probe on WB_3Prev
  // regfile_new_main main_6: pin names not known; wires that end beside it: BusA_ID, BusB_ID
  // Probe on multiplexer_4_out
  Multiplexer #(.select(2), .width(32), .enable("false")) multiplexer_3 (
    .in1(imm16_32_wb), .in2(main_10_out_11), .in3(bit_extender_4_out), .out(WB_3Prev), .sel(rd_src_WB));  // open: in0
  // Probe on BusB_ID
  assign bit_extender_4_out = {{12{PC_plus_1_WB[19]}}, PC_plus_1_WB};  // Bit_Extender bit_extender_4
  // Probe on imm16_32_wb
  block1 block1_1 (.op_code(opcode), .ALU_OP(ALU_OP), .func(func_4bit));
  // Probe on ALU_OP
  Multiplexer #(.width(32), .enable("false")) multiplexer_4 (
    .in0(WB_3Prev), .in1({WB_3Prev[15:0], imm16_16bit_mem}), .out(multiplexer_4_out), .sel(SSET_MEM));
  // Probe on multiplexer_4_out
  Multiplexer #(.select(2), .width(32), .enable("false")) multiplexer_5 (
    .in0(BusA_ID), .in1(ALU_res_EX), .in2(mem_2prev), .in3(WB_3Prev), .out(multiplexer_5_out), .sel(Forward_A));
  Multiplexer #(.select(2), .width(32), .enable("false")) multiplexer_6 (
    .in0(BusB_ID), .in1(ALU_res_EX), .in2(mem_2prev), .in3(WB_3Prev), .out(multiplexer_6_out), .sel(Forwad_B));
  // Probe on main_10_out_11
  // Probe on multiplexer_5_out
  // Probe on multiplexer_6_out
  // Probe on imm16_16bit_mem
  // Probe on WB_3Prev
  // Probe on ALU_SRC
  id_ex_main main_7 (
    .in_1(clock_1_out), .imm16(multiplexer_2_out), .BusA(multiplexer_5_out), .BusB(multiplexer_6_out),
    .Rs(Rs_ID), .Rt(Rt_ID), .PC_plus_1(PC_Plus_1_ID), .MEM_Read(MEM_Read), .MEM_Write(MEM_Write), .WB(WB),
    .Reg_Write(Reg_write), .Reg_Des(Rd_SRC), .RD(immd_L), .out_19({imm16_32_EX, imm16_16bit_EX}),
    .out_22(main_7_out_22), .out_23(BUSB_EX), .out_24(Rs_EX), .out_25(Rt_EX), .out_26(PC_Plus_1_EX),
    .out_27(MEM_Read_EX), .out_28(MEM_Write_EX), .out_29(WB_EX), .out_30(Reg_write_EX), .out_31(Rd_SRC_EX),
    .out_32(RD_EX), .ALU_OP(ALU_OP), .out_33(ALU_OP_EX), .ALU_SRC(ALU_SRC), .out_34(ALU_SRC_EX),
    .ImmL(immd_L), .out_20(immd_L_EX), .ImmU({imm16[15:9], func_4bit}), .out_21(immd_U_EX), .SSET(SSET),
    .out_35(SSET_EX));
  // Probe on ALU_SRC_EX
  // Probe on ALU_SRC_EX
  // Probe on {imm16_32_EX, imm16_16bit_EX}
  // Probe on main_7_out_22
  Multiplexer #(.select(2), .width(32), .enable("false")) multiplexer_7 (
    .in0({imm16_32_EX, imm16_16bit_EX}), .in1(BUSB_EX), .in2(immdL_immdU_EX), .out(multiplexer_7_out),
    .sel(ALU_SRC_EX));  // open: in3
  // Probe on multiplexer_7_out
  ALU alu_1 (
    .ALU_Result(ALU_res_EX), .less_flag_unsign(less_falg), .less_flag(less_Unsign_falg),
    .Zero_flag(Zero_flag), .A(main_7_out_22), .B(multiplexer_7_out), .ALU_Opration(ALU_OP_EX));  // open: Overflow
  // Probe on ALU_res_EX
  // Probe on {imm16_32_EX, imm16_16bit_EX}
  ex_mem_main main_8 (
    .in_1(clock_1_out), .WB(WB_EX), .MEM_Read(MEM_Read_EX), .MEM_Write(MEM_Write_EX),
    .Reg_write(Reg_write_EX), .Rd_src(Rd_SRC_EX), .PC_plus_1(PC_Plus_1_EX), .Rd(RD_EX), .Alu_res(ALU_res_EX),
    .out_14(WB_mem), .out_15(MEM_Read_mem), .out_16(MEM_Write_mem), .out_17(reg_write_mem),
    .out_18(rd_src_mem), .out_19(pc_plus_1_mem), .out_20(rd_mem), .out_21(Alu_res_mem),
    .imm16_16bit_EX(imm16_16bit_EX), .out_22(imm16_16bit_mem), .imm16_32_EX({imm16_32_EX, imm16_16bit_EX}),
    .out_23(imm16_32_mem), .BUSB_EX(BUSB_EX), .out_24(BUSB_mem), .SSET(SSET_EX), .out_25(SSET_MEM));
  // Probe on imm16_32_mem
  // Probe on BUSB_mem
  Data_Mem_main main_9 (
    .Mem_Write(MEM_Write_mem), .Mem_Read(MEM_Read_mem), .Clk(clock_1_out), .Data_In(BUSB_mem),
    .Data_Out(main_9_data_out), .Alu_Result(Alu_res_mem));
  Multiplexer #(.width(32), .enable("false")) multiplexer_8 (
    .in0(Alu_res_mem), .in1(main_9_data_out), .out(mem_2prev), .sel(WB_mem));
  // Probe on imm16_32_mem
  mem_wb_main main_10 (
    .reg_write(reg_write_mem), .rd_src(rd_src_mem), .PC_Plus_1(pc_plus_1_mem), .rd(rd_mem),
    .clk(clock_1_out), .out_12(reg_write_WB), .out_13(rd_src_WB), .out_14(PC_plus_1_WB), .out_15(rd_WB),
    .ALUres_or_DataOut(mem_2prev), .out_11(main_10_out_11), .imm16_16bit_mem(imm16_16bit_mem),
    .out_16(imm16_16bit_wb), .imm16_32_mem(imm16_32_mem), .out_17(imm16_32_wb), .BUSB_mem(BUSB_mem),
    .out_18(BUSB_wb), .SSET(SSET_MEM), .out_19(SSET_WB));
  // Probe on imm16_32_wb

  // Other names for the same wires on the sheet: RD_ID[4:0] = immd_L; imm16[8:5] = func_4bit;
  //   immd_U[10:0] = {imm16[15:9], func_4bit}; imm16_32_EX[15:0] = imm16_16bit_EX; R0[31:0] = out_1; R1[31:0] = out_2;
  //   R2[31:0] = out_3; R3[31:0] = out_4; R4[31:0] = out_5; R5[31:0] = out_6; R6[31:0] = out_7; R7[31:0] = out_8;
  //   R8[31:0] = out_9; R9[31:0] = out_10; R10[31:0] = out_11; R11[31:0] = out_12; R12[31:0] = out_13;
  //   R13[31:0] = out_14; R14[31:0] = out_15; R15[31:0] = out_16; R16[31:0] = out_17; R17[31:0] = out_18;
  //   R18[31:0] = out_19; R19[31:0] = out_20; R20[31:0] = out_21; R21[31:0] = out_22; R22[31:0] = out_23;
  //   R23[31:0] = out_24; R24[31:0] = out_25; R25[31:0] = out_26; R26[31:0] = out_27; R27[31:0] = out_28;
  //   R28[31:0] = out_29; R29[31:0] = out_30; R30[31:0] = out_31; R31[31:0] = out_32; x[31:0] = WB_3Prev

  // Notes on the sheet:
  //   IF_ID
  //   op_code
  //   function
  //   01-> SET
  //   10->ALU_Result
  //   ID_EX
  //   EX_MEM
  //   MEM_WB
endmodule
