// Logisim project ex_mem.circ as structural Verilog: 2 circuits, main circuit main
module main (
  input  in_1,
  input  in_2,
  input  WB,
  input  MEM_Read,
  input  MEM_Write,
  input  Reg_write,
  input  [1:0] Rd_src,
  input  [19:0] PC_plus_1,
  input  [4:0] Rd,
  input  [31:0] Bus_B,
  input  [31:0] Alu_res,
  output out_12,
  output out_13,
  output out_14,
  output out_15,
  output [1:0] out_16,
  output [19:0] out_17,
  output [4:0] out_18,
  output [31:0] out_19,
  output [31:0] out_20
);

  wire Stall;

  not not_1 (Stall, in_2);
  Register #(.width(1)) register_1 (.D(WB), .en(Stall), .clk(in_1), .Q(out_12));  // open: clr
  Register #(.width(1)) register_2 (.D(MEM_Read), .en(Stall), .clk(in_1), .Q(out_13));  // open: clr
  Register #(.width(1)) register_3 (.D(MEM_Write), .en(Stall), .clk(in_1), .Q(out_14));  // open: clr
  Register #(.width(1)) register_4 (.D(Reg_write), .en(Stall), .clk(in_1), .Q(out_15));  // open: clr
  Register #(.width(2)) register_5 (.D(Rd_src), .en(Stall), .clk(in_1), .Q(out_16));  // open: clr
  Register #(.width(20)) register_6 (.D(PC_plus_1), .en(Stall), .clk(in_1), .Q(out_17));  // open: clr
  Register #(.width(5)) register_7 (.D(Rd), .en(Stall), .clk(in_1), .Q(out_18));  // open: clr
  Register #(.width(32)) register_8 (.D(Bus_B), .en(Stall), .clk(in_1), .Q(out_19));  // open: clr
  Register #(.width(32)) register_9 (.D(Alu_res), .en(Stall), .clk(in_1), .Q(out_20));  // open: clr

  // Other names for the same wires on the sheet: CLk = in_1

  // Notes on the sheet:
  //   WB
  //   Mem_read
  //   mem_Write
  //   reg_wreite
  //   Rd_src
  //   pc+1
  //   Rd
  //   bus B
  //   alu_res
endmodule

module block (
);

  main main_1 ();  // open: in_1, in_2, WB, MEM_Read, MEM_Write, Reg_write, Rd_src, PC_plus_1, Rd, Bus_B, Alu_res, out_12, out_13, out_14, out_15, out_16, out_17, out_18, out_19, out_20
endmodule
