// Logisim project id_ex.circ as structural Verilog: 2 circuits, main circuit main
module main (
  input  in_1,
  input  [31:0] imm16,
  input  [31:0] immL_immU,
  input  [31:0] BusA,
  input  [31:0] BusB,
  input  [4:0] Rs,
  input  [4:0] Rt,
  input  [19:0] PC_plus_1,
  input  MEM_Read,
  input  MEM_Write,
  input  WB,
  input  Reg_Write,
  input  [1:0] Reg_Des,
  input  [4:0] RD,
  input  [9:0] ALU_OP,
  input  [1:0] ALU_SRC,
  output [31:0] out_17,
  output [31:0] out_18,
  output [31:0] out_19,
  output [31:0] out_20,
  output [4:0] out_21,
  output [4:0] out_22,
  output [19:0] out_23,
  output out_24,
  output out_25,
  output out_26,
  output out_27,
  output [1:0] out_28,
  output [4:0] out_29,
  output [9:0] out_30,
  output [1:0] out_31
);

  Register #(.width(32)) register_1 (.D(imm16), .en(1'b1), .clk(in_1), .Q(out_17));  // open: clr
  Register #(.width(32)) register_2 (.D(immL_immU), .en(1'b1), .clk(in_1), .Q(out_18));  // open: clr
  Register #(.width(32)) register_3 (.D(BusA), .en(1'b1), .clk(in_1), .Q(out_19));  // open: clr
  Register #(.width(32)) register_4 (.D(BusB), .en(1'b1), .clk(in_1), .Q(out_20));  // open: clr
  Register #(.width(5)) register_5 (.D(Rs), .en(1'b1), .clk(in_1), .Q(out_21));  // open: clr
  Register #(.width(5)) register_6 (.D(Rt), .en(1'b1), .clk(in_1), .Q(out_22));  // open: clr
  Register #(.width(20)) register_7 (.D(PC_plus_1), .en(1'b1), .clk(in_1), .Q(out_23));  // open: clr
  Register #(.width(1)) register_8 (.D(MEM_Read), .en(1'b1), .clk(in_1), .Q(out_24));  // open: clr
  Register #(.width(1)) register_9 (.D(MEM_Write), .en(1'b1), .clk(in_1), .Q(out_25));  // open: clr
  Register #(.width(1)) register_10 (.D(WB), .en(1'b1), .clk(in_1), .Q(out_26));  // open: clr
  Register #(.width(1)) register_11 (.D(Reg_Write), .en(1'b1), .clk(in_1), .Q(out_27));  // open: clr
  Register #(.width(2)) register_12 (.D(Reg_Des), .en(1'b1), .clk(in_1), .Q(out_28));  // open: clr
  Register #(.width(5)) register_13 (.D(RD), .en(1'b1), .clk(in_1), .Q(out_29));  // open: clr
  Register #(.width(10)) register_14 (.D(ALU_OP), .en(1'b1), .clk(in_1), .Q(out_30));  // open: clr
  Register #(.width(2)) register_15 (.D(ALU_SRC), .en(1'b1), .clk(in_1), .Q(out_31));  // open: clr

  // Other names for the same wires on the sheet: ClK = in_1

  // Notes on the sheet:
  //   imm16
  //   imml/imml
  //   busA
  //   bysb
  //   rs
  //   rt
  //   rd
  //   pc+1
  //   memread
  //   memwriete
  //   wb
  //   regwrite
  //   regdest
endmodule

module block (
);

  main main_1 ();  // open: in_1, imm16, immL_immU, BusA, BusB, Rs, Rt, PC_plus_1, MEM_Read, MEM_Write, WB, Reg_Write, Reg_Des, RD, out_17, out_18, out_19, out_20, out_21, out_22, out_23, out_24, out_25, out_26, out_27, out_28, out_29, ALU_OP, out_30, ALU_SRC, out_31
endmodule
