// Logisim project if_id.circ as structural Verilog: 2 circuits, main circuit main
module main (
  input  [31:0] Instruction,
  input  [19:0] PC_plus_1,
  input  in_3,
  output [31:0] out_4,
  output [19:0] out_5
);

  Register #(.width(32)) register_1 (.D(Instruction), .en(1'b1), .clk(in_3), .Q(out_4));  // open: clr
  Register #(.width(20)) register_2 (.D(PC_plus_1), .en(1'b1), .clk(in_3), .Q(out_5));  // open: clr
endmodule

module block (
);

  main main_1 ();  // open: Instruction, PC_plus_1, out_4, out_5, in_3
endmodule
