// Logisim project mem_wb.circ as structural Verilog: 2 circuits, main circuit main
module main (
  input  [31:0] ALUres_or_DataOut,
  input  reg_write,
  input  [4:0] rd,
  input  clk,
  output [31:0] out_5,
  output out_6,
  output [4:0] out_7
);

  Register #(.width(32)) register_1 (.D(ALUres_or_DataOut), .en(1'b1), .clk(clk), .Q(out_5));  // open: clr
  Register #(.width(1)) register_2 (.D(reg_write), .en(1'b1), .clk(clk), .Q(out_6));  // open: clr
  Register #(.width(5)) register_3 (.D(rd), .en(1'b1), .clk(clk), .Q(out_7));  // open: clr
endmodule

module bllock (
);

  main main_1 ();  // open: reg_write, rd, clk, out_6, out_7, ALUres_or_DataOut, out_5
endmodule
