// Logisim project pc_new.circ as structural Verilog: 2 circuits, main circuit main
module main (
  input  [1:0] Pc_Selctor,
  input  [15:0] Imm16,
  input  [31:0] RS1,
  input  [10:0] Immu,
  input  [4:0] ImmL,
  output [19:0] PC_Output
);

  wire clock_1_out;
  wire [19:0] adder_1_out, adder_3_out, bit_extender_2_out, PC_Count_q;
  wire [31:0] adder_2_out, bit_extender_1_out;

  Clock clock_1 (.out(clock_1_out));
  Register #(.width(20)) PC_Count (.D(PC_Output), .en(1'b1), .clk(clock_1_out), .Q(PC_Count_q));  // open: clr
  assign bit_extender_1_out = {{16{Imm16[15]}}, Imm16};  // Bit_Extender bit_extender_1
  assign bit_extender_2_out = {{4{Immu[10]}}, {Immu, ImmL}};  // Bit_Extender bit_extender_2
  Adder #(.width(20)) adder_1 (.a(PC_Count_q), .b(20'h1), .out(adder_1_out));  // open: cin, cout
  Adder #(.width(32)) adder_2 (.a(bit_extender_1_out), .b(RS1), .out(adder_2_out));  // open: cin, cout
  Adder #(.width(20)) adder_3 (.a(PC_Count_q), .b(bit_extender_2_out), .out(adder_3_out));  // open: cin, cout
  Multiplexer #(.select(2), .width(20), .enable("false")) multiplexer_1 (
    .in0(adder_1_out), .in1(adder_2_out[19:0]), .in2(adder_3_out), .out(PC_Output), .sel(Pc_Selctor));  // open: in3

  // Notes on the sheet:
  //   Next_PC
  //   Jump
  //   Branch
endmodule

module PC_BLOCK (
);

  main main_1 ();  // open: Pc_Selctor, Imm16, RS1, Immu, ImmL, PC_Output
endmodule
